// Digital circuit 2-bit Multiplier.dig as structural Verilog
module _2_bit_Multiplier (
  input  [1:0] A,
  input  [1:0] B,
  output P_0,
  output P_1,
  output P_2,
  output P_3
);

  wire and_3_out, and_4_out, or_1_out, or_2_out, or_3_out;

  and and_1 (P_0, A[0], B[0]);
  or or_1 (or_1_out, ~B[1], ~A[0]);  // Or
  or or_2 (or_2_out, ~A[1], ~B[0]);  // Or
  or or_3 (or_3_out, ~A[0], ~B[0]);  // Or
  and and_2 (P_3, B[0], A[0], B[1], A[1]);
  and and_3 (and_3_out, or_1_out, A[1], B[0]);
  and and_4 (and_4_out, or_2_out, B[1], A[0]);
  and and_5 (P_2, or_3_out, A[1], B[1]);
  or or_4 (P_1, and_3_out, and_4_out);

  // Notes on the sheet:
  //   2-bit Multiplier
endmodule
