// Digital circuit 4‑bit Ripple‑Carry Adder.dig as structural Verilog
module _4_bit_Ripple_Carry_Adder (
  input  Cin,
  input  [3:0] A,
  input  [3:0] B,
  output S_1,
  output S_2,
  output S_3,
  output S_4,
  output Cout
);

  wire and_1_out, and_2_out, and_3_out, and_4_out, and_5_out, and_6_out, and_7_out, and_8_out, or_1_out,
       or_2_out, or_3_out, xor_1_out, xor_2_out, xor_3_out, xor_4_out, xor_5_out, xor_6_out, xor_7_out,
       xor_8_out;

  xor xor_1 (xor_1_out, A[0], B[0]);
  and and_1 (and_1_out, A[0], B[0]);
  xor xor_2 (xor_2_out, A[0], B[0]);
  xor xor_3 (xor_3_out, A[1], B[1]);
  and and_2 (and_2_out, A[1], B[1]);
  xor xor_4 (xor_4_out, A[1], B[1]);
  xor xor_5 (xor_5_out, A[2], B[2]);
  and and_3 (and_3_out, A[2], B[2]);
  xor xor_6 (xor_6_out, A[2], B[2]);
  xor xor_7 (xor_7_out, A[3], B[3]);
  and and_4 (and_4_out, A[3], B[3]);
  xor xor_8 (xor_8_out, A[3], B[3]);
  xor xor_9 (S_1, xor_1_out, Cin);
  and and_5 (and_5_out, xor_2_out, Cin);
  xor xor_10 (S_2, xor_3_out, or_1_out);
  and and_6 (and_6_out, xor_4_out, or_1_out);
  xor xor_11 (S_3, xor_5_out, or_2_out);
  and and_7 (and_7_out, xor_6_out, or_2_out);
  xor xor_12 (S_4, xor_7_out, or_3_out);
  and and_8 (and_8_out, xor_8_out, or_3_out);
  or or_1 (or_1_out, and_1_out, and_5_out);
  or or_2 (or_2_out, and_2_out, and_6_out);
  or or_3 (or_3_out, and_3_out, and_7_out);
  or or_4 (Cout, and_4_out, and_8_out);

  // Notes on the sheet:
  //   4‑bit Ripple‑Carry Adder
endmodule
