// Digital circuit One Bit Adder.dig as structural Verilog
module One_Bit_Adder (
  input  A,
  input  B,
  input  Cin,
  output SUM,
  output Cout
);

  wire and_1_out, and_2_out, xor_1_out, xor_2_out;

  xor xor_1 (xor_1_out, A, B);
  and and_1 (and_1_out, A, B);
  xor xor_2 (xor_2_out, A, B);
  xor xor_3 (SUM, xor_1_out, Cin);
  and and_2 (and_2_out, xor_2_out, Cin);
  or or_1 (Cout, and_1_out, and_2_out);

  // Notes on the sheet:
  //   One Bit Adder
endmodule
